// Logisim project F3.circ as structural Verilog: 18 circuits, main circuit NOT_GATE
module NOT_GATE (
  input  in_1,
  output out_2
);

  Transistor transistor_1 (.in(1'b1), .out(out_2), .gate(in_1));
  Transistor #(.\type ("n")) transistor_2 (.in(1'b0), .out(out_2), .gate(in_1));
endmodule

module NAND_GATE (
  input  in_1,
  input  in_2,
  output out_3
);

  wire transistor_4_out;

  Transistor transistor_1 (.in(1'b1), .out(out_3), .gate(in_1));
  Transistor transistor_2 (.in(1'b1), .out(out_3), .gate(in_2));
  Transistor #(.\type ("n")) transistor_3 (.in(transistor_4_out), .out(out_3), .gate(in_1));
  Transistor #(.\type ("n")) transistor_4 (.in(1'b0), .out(transistor_4_out), .gate(in_2));
endmodule

module NAND_GATE2 (
  input  in_1,
  input  in_2,
  output out_3
);

  wire transistor_2_out;

  Transistor #(.\type ("n")) transistor_1 (.in(1'b0), .out(out_3), .gate(in_1));
  Transistor transistor_2 (.in(1'b1), .out(transistor_2_out), .gate(in_1));
  Transistor transistor_3 (.in(transistor_2_out), .out(out_3), .gate(in_2));
  Transistor #(.\type ("n")) transistor_4 (.in(1'b0), .out(out_3), .gate(in_2));
endmodule

module AND_GATE (
  input  in_1,
  input  in_2,
  output out_3
);

  wire transistor_1_out, transistor_4_out;

  Transistor transistor_1 (.in(1'b1), .out(transistor_1_out), .gate(in_1));
  Transistor transistor_2 (.in(1'b1), .out(transistor_1_out), .gate(in_2));
  Transistor #(.\type ("n")) transistor_3 (.in(transistor_4_out), .out(transistor_1_out), .gate(in_1));
  Transistor #(.\type ("n")) transistor_4 (.in(1'b0), .out(transistor_4_out), .gate(in_2));
  Transistor transistor_5 (.in(1'b1), .out(out_3), .gate(transistor_1_out));
  Transistor #(.\type ("n")) transistor_6 (.in(1'b0), .out(out_3), .gate(transistor_1_out));
endmodule

module NOR_GATE (
  input  in_1,
  input  in_2,
  output out_3
);

  wire transistor_2_out;

  Transistor #(.\type ("n")) transistor_1 (.in(1'b0), .out(out_3), .gate(in_2));
  Transistor transistor_2 (.in(1'b1), .out(transistor_2_out), .gate(in_1));
  Transistor transistor_3 (.in(transistor_2_out), .out(out_3), .gate(in_2));
  Transistor #(.\type ("n")) transistor_4 (.in(1'b0), .out(out_3), .gate(in_1));
endmodule

module OR_GATE (
  input  in_1,
  input  in_2,
  output out_3
);

  wire transistor_1_out, transistor_2_out;

  Transistor #(.\type ("n")) transistor_1 (.in(1'b0), .out(transistor_1_out), .gate(in_2));
  Transistor transistor_2 (.in(1'b1), .out(transistor_2_out), .gate(in_1));
  Transistor transistor_3 (.in(transistor_2_out), .out(transistor_1_out), .gate(in_2));
  Transistor transistor_4 (.in(1'b1), .out(out_3), .gate(transistor_1_out));
  Transistor #(.\type ("n")) transistor_5 (.in(1'b0), .out(transistor_1_out), .gate(in_1));
  Transistor #(.\type ("n")) transistor_6 (.in(1'b0), .out(out_3), .gate(transistor_1_out));
endmodule

module XOR_GATE (
  input  in_1,
  input  in_2,
  output out_3
);

  wire nand_1_out, or_1_out;

  nand nand_1 (nand_1_out, in_1, in_2);
  or or_1 (or_1_out, in_1, in_2);
  and and_1 (out_3, nand_1_out, or_1_out);
endmodule

module Decoder_2_4 (
  input  a1,
  input  a0,
  output b0,
  output b1,
  output b2,
  output b3
);

  wire not_1_out, not_2_out, not_3_out, not_4_out;

  not not_1 (not_1_out, a1);
  not not_2 (not_2_out, a0);
  not not_3 (not_3_out, a1);
  not not_4 (not_4_out, a0);
  and and_1 (b0, not_1_out, not_2_out);
  and and_2 (b1, not_3_out, a0);
  and and_3 (b2, a1, not_4_out);
  and and_4 (b3, a1, a0);
endmodule

module Decoder_3_8 (
  input  a1,
  input  a0,
  input  a2,
  output b0,
  output b1,
  output b2,
  output b3,
  output b4,
  output b5,
  output b6,
  output b7
);

  wire decoder_2_4_1_b0, decoder_2_4_1_b1, decoder_2_4_1_b2, decoder_2_4_1_b3, decoder_2_4_2_b0,
       decoder_2_4_2_b1, decoder_2_4_2_b2, decoder_2_4_2_b3, not_1_out;

  Decoder_2_4 decoder_2_4_1 (
    .a1(a1), .a0(a0), .b0(decoder_2_4_1_b0), .b1(decoder_2_4_1_b1), .b2(decoder_2_4_1_b2),
    .b3(decoder_2_4_1_b3));
  Decoder_2_4 decoder_2_4_2 (
    .a1(a1), .a0(a0), .b0(decoder_2_4_2_b0), .b1(decoder_2_4_2_b1), .b2(decoder_2_4_2_b2),
    .b3(decoder_2_4_2_b3));
  not not_1 (not_1_out, a2);
  and and_1 (b0, decoder_2_4_1_b0, not_1_out);
  and and_2 (b1, decoder_2_4_1_b1, not_1_out);
  and and_3 (b2, decoder_2_4_1_b2, not_1_out);
  and and_4 (b3, decoder_2_4_1_b3, not_1_out);
  and and_5 (b4, a2, decoder_2_4_2_b0);
  and and_6 (b5, a2, decoder_2_4_2_b1);
  and and_7 (b6, a2, decoder_2_4_2_b2);
  and and_8 (b7, a2, decoder_2_4_2_b3);
endmodule

module Decoder_4_16 (
  input  a0,
  input  a1,
  input  a2,
  input  a3,
  output b0,
  output b1,
  output b2,
  output b3,
  output b4,
  output b5,
  output b6,
  output b7,
  output b8,
  output b9,
  output ba,
  output bb,
  output bc,
  output bd,
  output be,
  output bf
);

  wire decoder_3_8_1_b0, decoder_3_8_1_b1, decoder_3_8_1_b2, decoder_3_8_1_b3, decoder_3_8_1_b4,
       decoder_3_8_1_b5, decoder_3_8_1_b6, decoder_3_8_1_b7, decoder_3_8_2_b0, decoder_3_8_2_b1,
       decoder_3_8_2_b2, decoder_3_8_2_b3, decoder_3_8_2_b4, decoder_3_8_2_b5, decoder_3_8_2_b6,
       decoder_3_8_2_b7, not_1_out;

  Decoder_3_8 decoder_3_8_1 (
    .a1(a1), .a0(a0), .a2(a2), .b0(decoder_3_8_1_b0), .b1(decoder_3_8_1_b1), .b2(decoder_3_8_1_b2),
    .b3(decoder_3_8_1_b3), .b4(decoder_3_8_1_b4), .b5(decoder_3_8_1_b5), .b6(decoder_3_8_1_b6),
    .b7(decoder_3_8_1_b7));
  not not_1 (not_1_out, a3);
  Decoder_3_8 decoder_3_8_2 (
    .a1(a1), .a0(a0), .a2(a2), .b0(decoder_3_8_2_b0), .b1(decoder_3_8_2_b1), .b2(decoder_3_8_2_b2),
    .b3(decoder_3_8_2_b3), .b4(decoder_3_8_2_b4), .b5(decoder_3_8_2_b5), .b6(decoder_3_8_2_b6),
    .b7(decoder_3_8_2_b7));
  and and_1 (b0, decoder_3_8_1_b0, not_1_out);
  and and_2 (b1, decoder_3_8_1_b1, not_1_out);
  and and_3 (b2, decoder_3_8_1_b2, not_1_out);
  and and_4 (b3, decoder_3_8_1_b3, not_1_out);
  and and_5 (b4, decoder_3_8_1_b4, not_1_out);
  and and_6 (b5, decoder_3_8_1_b5, not_1_out);
  and and_7 (b6, decoder_3_8_1_b6, not_1_out);
  and and_8 (b7, decoder_3_8_1_b7, not_1_out);
  and and_9 (b8, a3, decoder_3_8_2_b0);
  and and_10 (b9, a3, decoder_3_8_2_b1);
  and and_11 (ba, a3, decoder_3_8_2_b2);
  and and_12 (bb, a3, decoder_3_8_2_b3);
  and and_13 (bc, a3, decoder_3_8_2_b4);
  and and_14 (bd, a3, decoder_3_8_2_b5);
  and and_15 (be, a3, decoder_3_8_2_b6);
  and and_16 (bf, a3, decoder_3_8_2_b7);
endmodule

module Tube16_Onehot (
  input  a0,
  input  a1,
  input  a2,
  input  a3,
  input  a4,
  input  a5,
  input  a6,
  input  a7,
  input  a8,
  input  a9,
  input  aa,
  input  ab,
  input  ac,
  input  ad,
  input  ae,
  input  af,
  output b0,
  output b1,
  output b2,
  output b3,
  output b4,
  output b5,
  output b6
);

  or or_1 (b0, a0, a1, a2, a3, a4, a7, a8, a9, aa, ad);
  or or_2 (b1, a0, a2, a3, a5, a6, a7, a8, a9, aa, ac, ae, af);
  or or_3 (b2, a0, a4, a5, a6, a8, a9, aa, ab, ac, ae, af);
  or or_4 (b3, a2, a3, a4, a5, a6, a8, a9, aa, ab, ad, ae, af);
  or or_5 (b4, a0, a2, a6, a8, aa, ab, ac, ad, ae, af);
  or or_6 (b5, a0, a2, a3, a5, a6, a8, a9, ab, ac, ad, ae);
  or or_7 (b6, a0, a1, a3, a4, a5, a6, a7, a8, a9, aa, ab, ad);
endmodule

module Tube4_16 (
  input  a1,
  input  a0,
  input  a2,
  input  a4
);

  wire and_1_out, and_2_out, and_3_out, and_4_out, and_5_out, and_6_out, and_7_out, and_8_out, and_9_out,
       and_10_out, and_11_out, and_12_out, and_13_out, and_14_out, and_15_out, and_16_out, decoder_3_8_1_b0,
       decoder_3_8_1_b1, decoder_3_8_1_b2, decoder_3_8_1_b3, decoder_3_8_1_b4, decoder_3_8_1_b5,
       decoder_3_8_1_b6, decoder_3_8_1_b7, decoder_3_8_2_b0, decoder_3_8_2_b1, decoder_3_8_2_b2,
       decoder_3_8_2_b3, decoder_3_8_2_b4, decoder_3_8_2_b5, decoder_3_8_2_b6, decoder_3_8_2_b7, not_1_out,
       tube16_onehot_1_b0, tube16_onehot_1_b1, tube16_onehot_1_b2, tube16_onehot_1_b3, tube16_onehot_1_b4,
       tube16_onehot_1_b5, tube16_onehot_1_b6;

  Decoder_3_8 decoder_3_8_1 (
    .a1(a1), .a0(a0), .a2(a2), .b0(decoder_3_8_1_b0), .b1(decoder_3_8_1_b1), .b2(decoder_3_8_1_b2),
    .b3(decoder_3_8_1_b3), .b4(decoder_3_8_1_b4), .b5(decoder_3_8_1_b5), .b6(decoder_3_8_1_b6),
    .b7(decoder_3_8_1_b7));
  not not_1 (not_1_out, a4);
  Decoder_3_8 decoder_3_8_2 (
    .a1(a1), .a0(a0), .a2(a2), .b0(decoder_3_8_2_b0), .b1(decoder_3_8_2_b1), .b2(decoder_3_8_2_b2),
    .b3(decoder_3_8_2_b3), .b4(decoder_3_8_2_b4), .b5(decoder_3_8_2_b5), .b6(decoder_3_8_2_b6),
    .b7(decoder_3_8_2_b7));
  and and_1 (and_1_out, decoder_3_8_1_b0, not_1_out);
  and and_2 (and_2_out, decoder_3_8_1_b1, not_1_out);
  and and_3 (and_3_out, decoder_3_8_1_b2, not_1_out);
  and and_4 (and_4_out, decoder_3_8_1_b3, not_1_out);
  and and_5 (and_5_out, decoder_3_8_1_b4, not_1_out);
  and and_6 (and_6_out, decoder_3_8_1_b5, not_1_out);
  and and_7 (and_7_out, decoder_3_8_1_b6, not_1_out);
  and and_8 (and_8_out, decoder_3_8_1_b7, not_1_out);
  and and_9 (and_9_out, a4, decoder_3_8_2_b0);
  and and_10 (and_10_out, a4, decoder_3_8_2_b1);
  and and_11 (and_11_out, a4, decoder_3_8_2_b2);
  and and_12 (and_12_out, a4, decoder_3_8_2_b3);
  and and_13 (and_13_out, a4, decoder_3_8_2_b4);
  and and_14 (and_14_out, a4, decoder_3_8_2_b5);
  and and_15 (and_15_out, a4, decoder_3_8_2_b6);
  and and_16 (and_16_out, a4, decoder_3_8_2_b7);
  Tube16_Onehot tube16_onehot_1 (
    .a0(and_1_out), .a1(and_2_out), .a2(and_3_out), .a3(and_4_out), .a4(and_5_out), .a5(and_6_out),
    .a6(and_7_out), .a7(and_8_out), .a8(and_9_out), .a9(and_10_out), .aa(and_11_out), .ab(and_12_out),
    .ac(and_13_out), .ad(and_14_out), .ae(and_15_out), .af(and_16_out), .b0(tube16_onehot_1_b0),
    .b1(tube16_onehot_1_b1), .b2(tube16_onehot_1_b2), .b3(tube16_onehot_1_b3), .b4(tube16_onehot_1_b4),
    .b5(tube16_onehot_1_b5), .b6(tube16_onehot_1_b6));
  _7_Segment_Display u_7_segment_display_1 (
    .g(tube16_onehot_1_b3), .f(tube16_onehot_1_b2), .a(tube16_onehot_1_b1), .b(tube16_onehot_1_b0),
    .e(tube16_onehot_1_b4), .d(tube16_onehot_1_b5), .c(tube16_onehot_1_b6), .dp(1'b0));
endmodule

module mux2 (
  input  D0,
  input  S,
  input  D1,
  output Y
);

  wire and_1_out, and_2_out, not_1_out;

  not not_1 (not_1_out, S);
  and and_1 (and_1_out, D0, not_1_out);
  and and_2 (and_2_out, S, D1);
  or or_1 (Y, and_1_out, and_2_out);
endmodule

module mux4 (
  input  D0,
  input  D1,
  input  D2,
  input  D3,
  input  S0,
  input  S1,
  output Y
);

  wire mux2_1_y, mux2_2_y;

  mux2 mux2_1 (.D0(D0), .S(S0), .D1(D1), .Y(mux2_1_y));
  mux2 mux2_2 (.D0(D2), .S(S0), .D1(D3), .Y(mux2_2_y));
  mux2 mux2_3 (.D0(mux2_1_y), .S(S1), .D1(mux2_2_y), .Y(Y));
endmodule

module FA (
  input  A,
  input  B,
  input  C_in,
  output S,
  output C
);

  wire and_1_out, and_2_out, and_3_out, xor_1_out;

  xor xor_1 (xor_1_out, A, B);
  and and_1 (and_1_out, A, B);
  and and_2 (and_2_out, B, C_in);
  and and_3 (and_3_out, C_in, A);
  xor xor_2 (S, xor_1_out, C_in);
  or or_1 (C, and_1_out, and_2_out, and_3_out);

  // Notes on the sheet:
  //   三输入异或门有问题
endmodule

module DLatch (
  input  D,
  input  WE,
  output Q,
  output Q_n
);

  wire and_1_out, and_2_out, not_1_out;

  not not_1 (not_1_out, D);
  and and_1 (and_1_out, not_1_out, WE);
  and and_2 (and_2_out, WE, D);
  nor nor_1 (Q, and_1_out, Q_n);
  nor nor_2 (Q_n, Q, and_2_out);
endmodule

module DFF (
  input  D,
  input  CLK,
  output Q
);

  wire dlatch_1_q, not_1_out;

  not not_1 (not_1_out, CLK);
  DLatch dlatch_1 (.D(D), .WE(not_1_out), .Q(dlatch_1_q));  // open: Q_n
  DLatch dlatch_2 (.D(dlatch_1_q), .WE(CLK), .Q(Q));  // open: Q_n
endmodule

module digital_clock (
  input  rst_n
);

  wire clk_out, comparator_1_eq, comparator_2_lt, comparator_3_eq, comparator_4_lt, comparator_5_eq,
       comparator_6_lt, comparator_7_eq, decoder_4_16_1_b0, decoder_4_16_1_b1, decoder_4_16_1_b2,
       decoder_4_16_1_b3, decoder_4_16_1_b4, decoder_4_16_1_b5, decoder_4_16_1_b6, decoder_4_16_1_b7,
       decoder_4_16_1_b8, decoder_4_16_1_b9, decoder_4_16_1_ba, decoder_4_16_1_bb, decoder_4_16_1_bc,
       decoder_4_16_1_bd, decoder_4_16_1_be, decoder_4_16_1_bf, decoder_4_16_2_b0, decoder_4_16_2_b1,
       decoder_4_16_2_b2, decoder_4_16_2_b3, decoder_4_16_2_b4, decoder_4_16_2_b5, decoder_4_16_2_b6,
       decoder_4_16_2_b7, decoder_4_16_2_b8, decoder_4_16_2_b9, decoder_4_16_2_ba, decoder_4_16_2_bb,
       decoder_4_16_2_bc, decoder_4_16_2_bd, decoder_4_16_2_be, decoder_4_16_2_bf, decoder_4_16_3_b0,
       decoder_4_16_3_b1, decoder_4_16_3_b2, decoder_4_16_3_b3, decoder_4_16_3_b4, decoder_4_16_3_b5,
       decoder_4_16_3_b6, decoder_4_16_3_b7, decoder_4_16_3_b8, decoder_4_16_3_b9, decoder_4_16_3_ba,
       decoder_4_16_3_bb, decoder_4_16_3_bc, decoder_4_16_3_bd, decoder_4_16_3_be, decoder_4_16_3_bf,
       decoder_4_16_4_b0, decoder_4_16_4_b1, decoder_4_16_4_b2, decoder_4_16_4_b3, decoder_4_16_4_b4,
       decoder_4_16_4_b5, decoder_4_16_4_b6, decoder_4_16_4_b7, decoder_4_16_4_b8, decoder_4_16_4_b9,
       decoder_4_16_4_ba, decoder_4_16_4_bb, decoder_4_16_4_bc, decoder_4_16_4_bd, decoder_4_16_4_be,
       decoder_4_16_4_bf, not_1_out, or_1_out, or_2_out, or_3_out, or_4_out, tube16_onehot_1_b0,
       tube16_onehot_1_b1, tube16_onehot_1_b2, tube16_onehot_1_b3, tube16_onehot_1_b4, tube16_onehot_1_b5,
       tube16_onehot_1_b6, tube16_onehot_2_b0, tube16_onehot_2_b1, tube16_onehot_2_b2, tube16_onehot_2_b3,
       tube16_onehot_2_b4, tube16_onehot_2_b5, tube16_onehot_2_b6, tube16_onehot_3_b0, tube16_onehot_3_b1,
       tube16_onehot_3_b2, tube16_onehot_3_b3, tube16_onehot_3_b4, tube16_onehot_3_b5, tube16_onehot_3_b6,
       tube16_onehot_4_b0, tube16_onehot_4_b1, tube16_onehot_4_b2, tube16_onehot_4_b3, tube16_onehot_4_b4,
       tube16_onehot_4_b5, tube16_onehot_4_b6;
  wire [3:0] adder_1_out, adder_2_out, adder_3_out, adder_4_out, register_1_q, register_2_q, register_3_q,
       register_4_q;

  Clock clk (.out(clk_out));
  not not_1 (not_1_out, rst_n);
  Tube16_Onehot tube16_onehot_1 (
    .a0(decoder_4_16_1_b0), .a1(decoder_4_16_1_b1), .a2(decoder_4_16_1_b2), .a3(decoder_4_16_1_b3),
    .a4(decoder_4_16_1_b4), .a5(decoder_4_16_1_b5), .a6(decoder_4_16_1_b6), .a7(decoder_4_16_1_b7),
    .a8(decoder_4_16_1_b8), .a9(decoder_4_16_1_b9), .aa(decoder_4_16_1_ba), .ab(decoder_4_16_1_bb),
    .ac(decoder_4_16_1_bc), .ad(decoder_4_16_1_bd), .ae(decoder_4_16_1_be), .af(decoder_4_16_1_bf),
    .b0(tube16_onehot_1_b0), .b1(tube16_onehot_1_b1), .b2(tube16_onehot_1_b2), .b3(tube16_onehot_1_b3),
    .b4(tube16_onehot_1_b4), .b5(tube16_onehot_1_b5), .b6(tube16_onehot_1_b6));
  Decoder_4_16 decoder_4_16_1 (
    .a0(register_4_q[0]), .a1(register_4_q[1]), .a2(register_4_q[2]), .a3(register_4_q[3]),
    .b0(decoder_4_16_1_b0), .b1(decoder_4_16_1_b1), .b2(decoder_4_16_1_b2), .b3(decoder_4_16_1_b3),
    .b4(decoder_4_16_1_b4), .b5(decoder_4_16_1_b5), .b6(decoder_4_16_1_b6), .b7(decoder_4_16_1_b7),
    .b8(decoder_4_16_1_b8), .b9(decoder_4_16_1_b9), .ba(decoder_4_16_1_ba), .bb(decoder_4_16_1_bb),
    .bc(decoder_4_16_1_bc), .bd(decoder_4_16_1_bd), .be(decoder_4_16_1_be), .bf(decoder_4_16_1_bf));
  Register #(.width(4)) register_1 (.D(adder_1_out), .en(1'b1), .clk(clk_out), .Q(register_1_q), .clr(or_1_out));
  or or_1 (or_1_out, not_1_out, comparator_1_eq);
  _7_Segment_Display u_7_segment_display_1 (
    .g(tube16_onehot_1_b3), .f(tube16_onehot_1_b2), .a(tube16_onehot_1_b1), .b(tube16_onehot_1_b0),
    .e(tube16_onehot_1_b4), .d(tube16_onehot_1_b5), .c(tube16_onehot_1_b6));  // open: dp
  Comparator #(.mode("unsigned"), .width(4)) comparator_1 (
    .a(register_1_q), .b(4'b1010), .eq(comparator_1_eq));  // open: gt, lt
  Adder #(.width(4)) adder_1 (.a(register_1_q), .b(4'b0001), .out(adder_1_out), .cin(1'b0));  // open: cout
  Tube16_Onehot tube16_onehot_2 (
    .a0(decoder_4_16_2_b0), .a1(decoder_4_16_2_b1), .a2(decoder_4_16_2_b2), .a3(decoder_4_16_2_b3),
    .a4(decoder_4_16_2_b4), .a5(decoder_4_16_2_b5), .a6(decoder_4_16_2_b6), .a7(decoder_4_16_2_b7),
    .a8(decoder_4_16_2_b8), .a9(decoder_4_16_2_b9), .aa(decoder_4_16_2_ba), .ab(decoder_4_16_2_bb),
    .ac(decoder_4_16_2_bc), .ad(decoder_4_16_2_bd), .ae(decoder_4_16_2_be), .af(decoder_4_16_2_bf),
    .b0(tube16_onehot_2_b0), .b1(tube16_onehot_2_b1), .b2(tube16_onehot_2_b2), .b3(tube16_onehot_2_b3),
    .b4(tube16_onehot_2_b4), .b5(tube16_onehot_2_b5), .b6(tube16_onehot_2_b6));
  Decoder_4_16 decoder_4_16_2 (
    .a0(register_3_q[0]), .a1(register_3_q[1]), .a2(register_3_q[2]), .a3(register_3_q[3]),
    .b0(decoder_4_16_2_b0), .b1(decoder_4_16_2_b1), .b2(decoder_4_16_2_b2), .b3(decoder_4_16_2_b3),
    .b4(decoder_4_16_2_b4), .b5(decoder_4_16_2_b5), .b6(decoder_4_16_2_b6), .b7(decoder_4_16_2_b7),
    .b8(decoder_4_16_2_b8), .b9(decoder_4_16_2_b9), .ba(decoder_4_16_2_ba), .bb(decoder_4_16_2_bb),
    .bc(decoder_4_16_2_bc), .bd(decoder_4_16_2_bd), .be(decoder_4_16_2_be), .bf(decoder_4_16_2_bf));
  Comparator #(.mode("unsigned"), .width(4)) comparator_2 (
    .a(register_1_q), .b(4'b0101), .lt(comparator_2_lt));  // open: gt, eq
  Register #(.width(4)) register_2 (
    .D(adder_2_out), .en(1'b1), .clk(comparator_2_lt), .Q(register_2_q), .clr(or_2_out));
  _7_Segment_Display u_7_segment_display_2 (
    .g(tube16_onehot_2_b3), .f(tube16_onehot_2_b2), .a(tube16_onehot_2_b1), .b(tube16_onehot_2_b0),
    .e(tube16_onehot_2_b4), .d(tube16_onehot_2_b5), .c(tube16_onehot_2_b6));  // open: dp
  or or_2 (or_2_out, not_1_out, comparator_3_eq);
  Comparator #(.mode("unsigned"), .width(4)) comparator_3 (
    .a(register_2_q), .b(4'b0110), .eq(comparator_3_eq));  // open: gt, lt
  LED led_1 ();  // open: in
  LED led_2 ();  // open: in
  Tube16_Onehot tube16_onehot_3 (
    .a0(decoder_4_16_3_b0), .a1(decoder_4_16_3_b1), .a2(decoder_4_16_3_b2), .a3(decoder_4_16_3_b3),
    .a4(decoder_4_16_3_b4), .a5(decoder_4_16_3_b5), .a6(decoder_4_16_3_b6), .a7(decoder_4_16_3_b7),
    .a8(decoder_4_16_3_b8), .a9(decoder_4_16_3_b9), .aa(decoder_4_16_3_ba), .ab(decoder_4_16_3_bb),
    .ac(decoder_4_16_3_bc), .ad(decoder_4_16_3_bd), .ae(decoder_4_16_3_be), .af(decoder_4_16_3_bf),
    .b0(tube16_onehot_3_b0), .b1(tube16_onehot_3_b1), .b2(tube16_onehot_3_b2), .b3(tube16_onehot_3_b3),
    .b4(tube16_onehot_3_b4), .b5(tube16_onehot_3_b5), .b6(tube16_onehot_3_b6));
  Decoder_4_16 decoder_4_16_3 (
    .a0(register_2_q[0]), .a1(register_2_q[1]), .a2(register_2_q[2]), .a3(register_2_q[3]),
    .b0(decoder_4_16_3_b0), .b1(decoder_4_16_3_b1), .b2(decoder_4_16_3_b2), .b3(decoder_4_16_3_b3),
    .b4(decoder_4_16_3_b4), .b5(decoder_4_16_3_b5), .b6(decoder_4_16_3_b6), .b7(decoder_4_16_3_b7),
    .b8(decoder_4_16_3_b8), .b9(decoder_4_16_3_b9), .ba(decoder_4_16_3_ba), .bb(decoder_4_16_3_bb),
    .bc(decoder_4_16_3_bc), .bd(decoder_4_16_3_bd), .be(decoder_4_16_3_be), .bf(decoder_4_16_3_bf));
  Adder #(.width(4)) adder_2 (.a(register_2_q), .b(4'b0001), .out(adder_2_out), .cin(1'b0));  // open: cout
  Comparator #(.mode("unsigned"), .width(4)) comparator_4 (
    .a(register_2_q), .b(4'b0011), .lt(comparator_4_lt));  // open: gt, eq
  _7_Segment_Display u_7_segment_display_3 (
    .g(tube16_onehot_3_b3), .f(tube16_onehot_3_b2), .a(tube16_onehot_3_b1), .b(tube16_onehot_3_b0),
    .e(tube16_onehot_3_b4), .d(tube16_onehot_3_b5), .c(tube16_onehot_3_b6));  // open: dp
  Register #(.width(4)) register_3 (
    .D(adder_3_out), .en(1'b1), .clk(comparator_4_lt), .Q(register_3_q), .clr(or_3_out));
  or or_3 (or_3_out, not_1_out, comparator_5_eq);
  Adder #(.width(4)) adder_3 (.a(register_3_q), .b(4'b0001), .out(adder_3_out), .cin(1'b0));  // open: cout
  Comparator #(.mode("unsigned"), .width(4)) comparator_5 (
    .a(register_3_q), .b(4'b1010), .eq(comparator_5_eq));  // open: gt, lt
  Tube16_Onehot tube16_onehot_4 (
    .a0(decoder_4_16_4_b0), .a1(decoder_4_16_4_b1), .a2(decoder_4_16_4_b2), .a3(decoder_4_16_4_b3),
    .a4(decoder_4_16_4_b4), .a5(decoder_4_16_4_b5), .a6(decoder_4_16_4_b6), .a7(decoder_4_16_4_b7),
    .a8(decoder_4_16_4_b8), .a9(decoder_4_16_4_b9), .aa(decoder_4_16_4_ba), .ab(decoder_4_16_4_bb),
    .ac(decoder_4_16_4_bc), .ad(decoder_4_16_4_bd), .ae(decoder_4_16_4_be), .af(decoder_4_16_4_bf),
    .b0(tube16_onehot_4_b0), .b1(tube16_onehot_4_b1), .b2(tube16_onehot_4_b2), .b3(tube16_onehot_4_b3),
    .b4(tube16_onehot_4_b4), .b5(tube16_onehot_4_b5), .b6(tube16_onehot_4_b6));
  Decoder_4_16 decoder_4_16_4 (
    .a0(register_1_q[0]), .a1(register_1_q[1]), .a2(register_1_q[2]), .a3(register_1_q[3]),
    .b0(decoder_4_16_4_b0), .b1(decoder_4_16_4_b1), .b2(decoder_4_16_4_b2), .b3(decoder_4_16_4_b3),
    .b4(decoder_4_16_4_b4), .b5(decoder_4_16_4_b5), .b6(decoder_4_16_4_b6), .b7(decoder_4_16_4_b7),
    .b8(decoder_4_16_4_b8), .b9(decoder_4_16_4_b9), .ba(decoder_4_16_4_ba), .bb(decoder_4_16_4_bb),
    .bc(decoder_4_16_4_bc), .bd(decoder_4_16_4_bd), .be(decoder_4_16_4_be), .bf(decoder_4_16_4_bf));
  Comparator #(.mode("unsigned"), .width(4)) comparator_6 (
    .a(register_3_q), .b(4'b0101), .lt(comparator_6_lt));  // open: gt, eq
  Register #(.width(4)) register_4 (
    .D(adder_4_out), .en(1'b1), .clk(comparator_6_lt), .Q(register_4_q), .clr(or_4_out));
  _7_Segment_Display u_7_segment_display_4 (
    .g(tube16_onehot_4_b3), .f(tube16_onehot_4_b2), .a(tube16_onehot_4_b1), .b(tube16_onehot_4_b0),
    .e(tube16_onehot_4_b4), .d(tube16_onehot_4_b5), .c(tube16_onehot_4_b6));  // open: dp
  or or_4 (or_4_out, not_1_out, comparator_7_eq);
  Comparator #(.mode("unsigned"), .width(4)) comparator_7 (
    .a(register_4_q), .b(4'b0110), .eq(comparator_7_eq));  // open: gt, lt
  Adder #(.width(4)) adder_4 (.a(register_4_q), .b(4'b0001), .out(adder_4_out), .cin(1'b0));  // open: cout
  Comparator #(.mode("unsigned"), .width(4)) comparator_8 (.a(register_4_q), .b(4'b0011));  // open: gt, eq, lt
endmodule
